# Fritzing sketch remoht-arduino (saved by Fritzing 0.7.11b)

parts:
  Arduino = Arduino Pro Mini 3.3V
  T1 = LM35 Temperature Sensor [package="TO92 [THT]"]
  LDR = Photocell (LDR) [package=THT]
  Relay_2 = LED - 5mm [color="Red (633nm)" package="5 mm [THT]"]
  Relay_1 = LED - 5mm [color="Red (633nm)" package="5 mm [THT]"]
  PIR = Infrared Proximity Sensor
  Power = Power plug
  R2 = Resistor [tolerance=±5% resistance=10k package=THT]

nets:
  VCC: Arduino.VCC, T1.+Vs, LDR.pin_1, PIR.Vcc, Power.VCC
  GND: Arduino.GND, T1.GND, Relay_2.cathode, Relay_1.cathode, PIR.GND, Power.GND, R2.Pin_0
  N1: Arduino.A1, T1.Vout
  N2: Arduino.A0, LDR.pin_0, R2.Pin_1
  N3: Arduino.D4, PIR.Vout
  N4: Arduino.D3, Relay_1.anode
  N5: Arduino.D2, Relay_2.anode

notes:
  Remoht.us Sensor Board
  Note: this assumes a regulated 5V input , which may note be the case...
